// Logisim project projeto de circuito.circ as structural Verilog
module Flip_flop_do_tipo_D (
  input  D,
  input  CLK,
  input  Enable,
  input  Preset,
  input  Clear,
  output Q
);

  wire and_1_out, and_2_out, and_3_out, nor_2_out, not_1_out, not_2_out, not_3_out, not_4_out, not_5_out,
       not_6_out;

  not not_1 (not_1_out, CLK);
  not not_2 (not_2_out, not_1_out);
  not not_3 (not_3_out, not_2_out);
  not not_4 (not_4_out, not_3_out);
  not not_5 (not_5_out, not_4_out);
  and and_1 (and_1_out, not_5_out, CLK, Enable);
  not not_6 (not_6_out, D);
  and and_2 (and_2_out, not_6_out, and_1_out);
  and and_3 (and_3_out, and_1_out, D);
  nor nor_1 (Q, and_2_out, Clear, nor_2_out);
  nor nor_2 (nor_2_out, Q, Preset, and_3_out);
endmodule

module \Cronômetro_16bits  (
  input  Clear,
  output out_2,
  output [3:0] out_3
);

  wire button_1_out, button_2_out, button_3_out, button_4_out, button_5_out, button_6_out, button_7_out,
       button_8_out, button_9_out, clock_1_out, \cronômetro_8bits_1_zero ;
  wire [3:0] \cronômetro_8bits_1_saida1 , \cronômetro_8bits_1_saida_2 , \cronômetro_8bits_2_proximo ,
       \cronômetro_8bits_2_saida1 , \cronômetro_8bits_2_saida_2 ;

  Button button_1 (.out(button_1_out));
  Clock clock_1 (.out(clock_1_out));
  Button button_2 (.out(button_2_out));
  Button button_3 (.out(button_3_out));
  Button button_4 (.out(button_4_out));
  Hex_Digit_Display hex_digit_display_1 (.value(\cronômetro_8bits_1_saida1 ));  // open: dp
  Hex_Digit_Display hex_digit_display_2 (.value(\cronômetro_8bits_1_saida_2 ));  // open: dp
  \Cronômetro_8bits  \cronômetro_8bits_1  (
    .CLK(clock_1_out), .Clear(Clear), .Zero(\cronômetro_8bits_1_zero ),
    .saida_2(\cronômetro_8bits_1_saida_2 ), .Proximo(out_3), .saida1(\cronômetro_8bits_1_saida1 ),
    .Pause(button_1_out), .in_2(\cronômetro_8bits_2_proximo ), .DSB(button_4_out), .DSA(button_3_out),
    .USA(button_5_out), .USB(button_2_out));
  Button button_5 (.out(button_5_out));
  LED led_1 (.in(\cronômetro_8bits_1_zero ));
  Hex_Digit_Display hex_digit_display_3 (.value(\cronômetro_8bits_2_proximo ));  // open: dp
  Hex_Digit_Display hex_digit_display_4 (.value(\cronômetro_8bits_2_saida_2 ));  // open: dp
  \Cronômetro_8bits  \cronômetro_8bits_2  (
    .CLK(clock_1_out), .Clear(Clear), .Zero(out_2), .saida_2(\cronômetro_8bits_2_saida_2 ),
    .Proximo(\cronômetro_8bits_2_proximo ), .saida1(\cronômetro_8bits_2_saida1 ), .Pause(button_1_out),
    .in_2(4'b0001), .DSB(button_7_out), .DSA(button_8_out), .USA(button_6_out), .USB(button_9_out));
  Button button_6 (.out(button_6_out));
  Button button_7 (.out(button_7_out));
  Hex_Digit_Display hex_digit_display_5 (.value(\cronômetro_8bits_2_saida1 ));  // open: dp
  Button button_8 (.out(button_8_out));
  Button button_9 (.out(button_9_out));
endmodule

module \Cronômetro_8bits  (
  input  CLK,
  input  [3:0] in_2,
  input  Clear,
  input  Pause,
  input  DSB,
  input  DSA,
  input  USA,
  input  USB,
  output Zero,
  output [3:0] saida_2,
  output [3:0] Proximo,
  output [3:0] saida1
);

  wire [3:0] and_1_out, not_1_out, not_2_out, somador_cronometro_v4_2_1_saida_1,
       somador_cronometro_v4_2_1_saida_2;

  Clock clock_1 ();  // open: out
  registrador_4_bits registrador_4_bits_1 (
    .in_1(somador_cronometro_v4_2_1_saida_2), .CLK(CLK), .Preset(1'b0), .Enable(1'b1), .Clear(Clear),
    .out_6(saida_2));
  Hex_Digit_Display hex_digit_display_1 (.value(saida_2));  // open: dp
  registrador_4_bits registrador_4_bits_2 (
    .in_1(somador_cronometro_v4_2_1_saida_1), .CLK(CLK), .Preset(1'b0), .Enable(1'b1), .Clear(Clear),
    .out_6(saida1));
  Hex_Digit_Display hex_digit_display_2 (.value(saida1));  // open: dp
  assign not_1_out = ~saida1;  // NOT_Gate not_1, 4 bits wide
  assign and_1_out = not_1_out & not_2_out;  // AND_Gate and_1, 4 bits wide
  assign not_2_out = ~saida_2;  // NOT_Gate not_2, 4 bits wide
  and and_2 (Zero, and_1_out[0], and_1_out[1], and_1_out[2], and_1_out[3]);
  Somador_cronometro_v4_2 somador_cronometro_v4_2_1 (
    .Entrada_1(saida1), .USA(USA), .USB(USB), .Pausa(Pause), .Clear(Clear), .in_7(saida_2), .DSA(DSA),
    .DSB(DSB), .Saida_1(somador_cronometro_v4_2_1_saida_1), .Saida_2(somador_cronometro_v4_2_1_saida_2),
    .out_12(Proximo), .Modificado(in_2));
endmodule

module registrador_4_bits (
  input  [3:0] in_1,
  input  CLK,
  input  Preset,
  input  Enable,
  input  Clear,
  output [3:0] out_6
);

  Flip_flop_do_tipo_D flip_flop_do_tipo_d_1 (
    .D(in_1[3]), .Enable(Enable), .Preset(Preset), .Clear(Clear), .Q(out_6[3]), .CLK(CLK));
  Flip_flop_do_tipo_D flip_flop_do_tipo_d_2 (
    .D(in_1[2]), .Enable(Enable), .Preset(Preset), .Clear(Clear), .Q(out_6[2]), .CLK(CLK));
  Flip_flop_do_tipo_D flip_flop_do_tipo_d_3 (
    .D(in_1[1]), .Enable(Enable), .Preset(Preset), .Clear(Clear), .Q(out_6[1]), .CLK(CLK));
  Flip_flop_do_tipo_D flip_flop_do_tipo_d_4 (
    .D(in_1[0]), .Enable(Enable), .Preset(Preset), .Clear(Clear), .Q(out_6[0]), .CLK(CLK));
endmodule

module passa1_segundos (
  input  [3:0] in_1,
  output [3:0] Saida,
  output [3:0] out_3
);

  and and_1 (out_3[0], ~in_1[0], in_1[1], ~in_1[2], in_1[3]);  // AND_Gate
  Mux mux_1 (.in_3(out_3[0]), .out_4(Saida), .in_1(in_1), .in_2(4'b0000));

  assign out_3[3:1] = 3'b000;
endmodule

module passa1_dezenas_sugundo (
  input  [3:0] in_1,
  output [3:0] Saida,
  output [3:0] out_3
);

  and and_1 (out_3[0], in_1[0], in_1[1], in_1[2], ~in_1[3]);  // AND_Gate
  Mux mux_1 (.in_3(out_3[0]), .out_4(Saida), .in_1(in_1), .in_2(4'b0000));

  assign out_3[3:1] = 3'b000;
endmodule

module Somador_cronometro_v4_2 (
  input  [3:0] Entrada_1,
  input  [3:0] Modificado,
  input  USA,
  input  USB,
  input  Pausa,
  input  Clear,
  input  [3:0] in_7,
  input  DSA,
  input  DSB,
  output [3:0] Saida_1,
  output [3:0] Saida_2,
  output [3:0] out_12
);

  wire A_out, and_1_out, and_2_out, and_3_out, and_4_out, and_5_out, and_6_out, botao_1_out_3, F_out,
       or_1_out;
  wire [0:0] and_7_out;
  wire [3:0] modificado_cronometro_1_out_5, modificado_cronometro_2_out_5, mux_1_out_4, mux_2_out_4,
       mux_3_out_4, mux_4_out_4, not_1_out, subtractor_1_out, subtractor_2_out;

  Botao botao_1 (.Botao(Pausa), .Clear(Clear), .out_3(botao_1_out_3));
  Subtractor #(.width(4)) subtractor_1 (.a(Entrada_1), .b(Modificado), .out(subtractor_1_out));  // open: bin, bout
  Subtractor #(.width(4)) subtractor_2 (
    .a(in_7), .b({3'b000, and_7_out[0]}), .out(subtractor_2_out));  // open: bin, bout
  Mux mux_1 (.in_3(botao_1_out_3), .out_4(mux_1_out_4), .in_1(subtractor_1_out), .in_2(Entrada_1));
  Mux mux_2 (.in_3(botao_1_out_3), .out_4(mux_2_out_4), .in_1(subtractor_2_out), .in_2(in_7));
  modificado_cronometro modificado_cronometro_1 (
    .Entrada(mux_1_out_4), .Ativo(botao_1_out_3), .Somar_1(USB), .Subtrair_1(USA),
    .out_5(modificado_cronometro_1_out_5));
  modificado_cronometro modificado_cronometro_2 (
    .Entrada(mux_2_out_4), .Ativo(botao_1_out_3), .Somar_1(DSB), .Subtrair_1(DSA),
    .out_5(modificado_cronometro_2_out_5));
  and F (F_out, modificado_cronometro_1_out_5[0], modificado_cronometro_1_out_5[1], modificado_cronometro_1_out_5[2], modificado_cronometro_1_out_5[3]);
  and A (A_out, ~modificado_cronometro_1_out_5[0], modificado_cronometro_1_out_5[1], ~modificado_cronometro_1_out_5[2], modificado_cronometro_1_out_5[3]);  // AND_Gate
  and and_1 (and_1_out, modificado_cronometro_2_out_5[0], modificado_cronometro_2_out_5[1], modificado_cronometro_2_out_5[2], modificado_cronometro_2_out_5[3]);
  and and_2 (and_2_out, ~modificado_cronometro_2_out_5[0], modificado_cronometro_2_out_5[1], modificado_cronometro_2_out_5[2], ~modificado_cronometro_2_out_5[3]);  // AND_Gate
  and and_3 (and_3_out, modificado_cronometro_2_out_5[0], modificado_cronometro_2_out_5[1], modificado_cronometro_2_out_5[2], ~modificado_cronometro_2_out_5[3]);  // AND_Gate
  Mux mux_3 (.in_3(F_out), .out_4(mux_3_out_4), .in_1(modificado_cronometro_1_out_5), .in_2(4'b1001));
  assign not_1_out = ~Modificado;  // NOT_Gate not_1, 4 bits wide
  Mux mux_4 (.in_3(and_1_out), .out_4(mux_4_out_4), .in_1(modificado_cronometro_2_out_5), .in_2(4'b0101));
  Mux mux_5 (.in_3(A_out), .out_4(Saida_1), .in_1(mux_3_out_4), .in_2(4'b0000));
  Mux mux_6 (.in_3(or_1_out), .out_4(Saida_2), .in_1(mux_4_out_4), .in_2(4'b0000));
  or or_1 (or_1_out, and_2_out, and_3_out);
  and and_4 (and_4_out, not_1_out[0], not_1_out[1], not_1_out[2], not_1_out[3]);
  and and_5 (and_5_out, Saida_1[0], ~Saida_1[1], ~Saida_1[2], Saida_1[3]);  // AND_Gate
  and and_6 (and_6_out, Saida_2[0], ~Saida_2[1], Saida_2[2], ~Saida_2[3]);  // AND_Gate
  and and_7 (and_7_out[0], and_5_out, ~and_4_out);  // AND_Gate
  and and_8 (out_12[0], and_7_out[0], and_6_out);

  assign out_12[3:1] = 3'b000;
endmodule

module modificado_cronometro (
  input  [3:0] Entrada,
  input  Ativo,
  input  Somar_1,
  input  Subtrair_1,
  output [3:0] out_5
);

  wire and_1_out, and_2_out, and_3_out, or_1_out;
  wire [3:0] adder_1_out, mux_2_out_4, subtractor_1_out;

  and and_1 (and_1_out, Ativo, Subtrair_1, ~Somar_1);  // AND_Gate
  or or_1 (or_1_out, and_1_out, and_2_out);
  and and_2 (and_2_out, Ativo, ~Subtrair_1, Somar_1);  // AND_Gate
  Adder #(.width(4)) adder_1 (.a(4'b0001), .b(Entrada), .out(adder_1_out));  // open: cin, cout
  Subtractor #(.width(4)) subtractor_1 (.a(Entrada), .b(4'b0001), .out(subtractor_1_out));  // open: bin, bout
  and and_3 (and_3_out, Ativo, Subtrair_1, ~Somar_1);  // AND_Gate
  Mux mux_1 (.in_3(or_1_out), .out_4(out_5), .in_1(Entrada), .in_2(mux_2_out_4));
  Mux mux_2 (.in_3(and_3_out), .out_4(mux_2_out_4), .in_1(adder_1_out), .in_2(subtractor_1_out));
endmodule

module Botao (
  input  Botao,
  input  Clear,
  output out_3
);

  wire not_1_out;

  not not_1 (not_1_out, out_3);
  Flip_flop_do_tipo_D flip_flop_do_tipo_d_1 (
    .D(not_1_out), .Enable(1'b1), .Preset(1'b0), .Clear(Clear), .Q(out_3), .CLK(Botao));
endmodule

module Somador_cronometro_v1 (
  input  [3:0] Entrada_1,
  input  [3:0] in_2,
  output [3:0] Saida_1,
  output [3:0] Saida_2,
  output [3:0] out_5
);

  wire [0:0] and_1_out;
  wire [3:0] adder_1_out, adder_2_out;

  Adder #(.width(4)) adder_1 (.a(4'b0001), .b(Entrada_1), .out(adder_1_out));  // open: cin, cout
  Adder #(.width(4)) adder_2 (.a({3'b000, and_1_out[0]}), .b(in_2), .out(adder_2_out));  // open: cin, cout
  and and_1 (and_1_out[0], ~adder_1_out[0], adder_1_out[1], ~adder_1_out[2], adder_1_out[3]);  // AND_Gate
  Mux mux_1 (.in_3(and_1_out[0]), .out_4(Saida_1), .in_1(adder_1_out), .in_2(4'b0000));
  and and_2 (out_5[0], ~adder_2_out[0], adder_2_out[1], adder_2_out[2], ~adder_2_out[3]);  // AND_Gate
  Mux mux_2 (.in_3(out_5[0]), .out_4(Saida_2), .in_1(adder_2_out), .in_2(4'b0000));

  assign out_5[3:1] = 3'b000;
endmodule

module Somador_cronometro_v2 (
  input  [3:0] Entrada_1,
  input  Pausa,
  input  [3:0] in_3,
  output [3:0] Saida_1,
  output [3:0] Saida_2,
  output [3:0] out_6
);

  wire [0:0] and_1_out;
  wire [3:0] adder_1_out, adder_2_out, mux_1_out_4, mux_2_out_4;

  Adder #(.width(4)) adder_1 (.a(4'b0001), .b(Entrada_1), .out(adder_1_out));  // open: cin, cout
  Adder #(.width(4)) adder_2 (.a({3'b000, and_1_out[0]}), .b(in_3), .out(adder_2_out));  // open: cin, cout
  Mux mux_1 (.in_3(Pausa), .out_4(mux_1_out_4), .in_1(adder_1_out), .in_2(Entrada_1));
  Mux mux_2 (.in_3(Pausa), .out_4(mux_2_out_4), .in_1(adder_2_out), .in_2(in_3));
  and and_1 (and_1_out[0], ~mux_1_out_4[0], mux_1_out_4[1], ~mux_1_out_4[2], mux_1_out_4[3]);  // AND_Gate
  Mux mux_3 (.in_3(and_1_out[0]), .out_4(Saida_1), .in_1(mux_1_out_4), .in_2(4'b0000));
  and and_2 (out_6[0], ~mux_2_out_4[0], mux_2_out_4[1], mux_2_out_4[2], ~mux_2_out_4[3]);  // AND_Gate
  Mux mux_4 (.in_3(out_6[0]), .out_4(Saida_2), .in_1(mux_2_out_4), .in_2(4'b0000));

  assign out_6[3:1] = 3'b000;
endmodule

module cronometro_v1 (
  input  CLK,
  input  Preset,
  input  Enable,
  input  Clear,
  output [3:0] out_5,
  output [3:0] out_6,
  output [3:0] saida_2,
  output [3:0] out_8,
  output [3:0] saida1
);

  wire button_1_out, button_2_out, button_3_out, button_4_out, button_5_out, clock_1_out;

  Clock clock_1 (.out(clock_1_out));
  registrador_4_bits registrador_4_bits_1 (
    .in_1(out_6), .CLK(clock_1_out), .Preset(Preset), .Enable(Enable), .Clear(Clear), .out_6(saida_2));
  Hex_Digit_Display hex_digit_display_1 (.value(saida_2));  // open: dp
  registrador_4_bits registrador_4_bits_2 (
    .in_1(out_5), .CLK(clock_1_out), .Preset(Preset), .Enable(Enable), .Clear(Clear), .out_6(saida1));
  Hex_Digit_Display hex_digit_display_2 (.value(saida1));  // open: dp
  Button button_1 (.out(button_1_out));
  Button button_2 (.out(button_2_out));
  Button button_3 (.out(button_3_out));
  Somador_cronometro_v3 somador_cronometro_v3_1 (
    .Modificado(4'b0001), .Entrada_1(saida1), .USA(button_5_out), .USB(button_4_out), .Pausa(button_1_out),
    .Clear(Clear), .in_7(saida_2), .DSA(button_3_out), .DSB(button_2_out), .Saida_1(out_5), .Saida_2(out_6),
    .out_12(out_8));
  Button button_4 (.out(button_4_out));
  Button button_5 (.out(button_5_out));
endmodule

module Somador_cronometro_v3 (
  input  [3:0] Modificado,
  input  [3:0] Entrada_1,
  input  USA,
  input  USB,
  input  Pausa,
  input  Clear,
  input  [3:0] in_7,
  input  DSA,
  input  DSB,
  output [3:0] Saida_1,
  output [3:0] Saida_2,
  output [3:0] out_12
);

  wire botao_1_out_3;
  wire [0:0] and_1_out;
  wire [3:0] adder_1_out, adder_2_out, mux_1_out_4, mux_2_out_4, mux_3_out_4, mux_4_out_4;

  Botao botao_1 (.Botao(Pausa), .Clear(Clear), .out_3(botao_1_out_3));
  Adder #(.width(4)) adder_1 (.a(Modificado), .b(Entrada_1), .out(adder_1_out));  // open: cin, cout
  Adder #(.width(4)) adder_2 (.a({3'b000, and_1_out[0]}), .b(in_7), .out(adder_2_out));  // open: cin, cout
  Mux mux_1 (.in_3(botao_1_out_3), .out_4(mux_1_out_4), .in_1(adder_1_out), .in_2(Entrada_1));
  Mux mux_2 (.in_3(botao_1_out_3), .out_4(mux_2_out_4), .in_1(adder_2_out), .in_2(in_7));
  and and_1 (and_1_out[0], ~mux_1_out_4[0], mux_1_out_4[1], ~mux_1_out_4[2], mux_1_out_4[3]);  // AND_Gate
  Mux mux_3 (.in_3(and_1_out[0]), .out_4(mux_3_out_4), .in_1(mux_1_out_4), .in_2(4'b0000));
  and and_2 (out_12[0], ~mux_2_out_4[0], mux_2_out_4[1], mux_2_out_4[2], ~mux_2_out_4[3]);  // AND_Gate
  Mux mux_4 (.in_3(out_12[0]), .out_4(mux_4_out_4), .in_1(mux_2_out_4), .in_2(4'b0000));
  modificado_cronometro modificado_cronometro_1 (
    .Entrada(mux_3_out_4), .Ativo(botao_1_out_3), .Somar_1(USB), .Subtrair_1(USA), .out_5(Saida_1));
  modificado_cronometro modificado_cronometro_2 (
    .Entrada(mux_4_out_4), .Ativo(botao_1_out_3), .Somar_1(DSB), .Subtrair_1(DSA), .out_5(Saida_2));

  assign out_12[3:1] = 3'b000;
endmodule
